// Logisim project cpu.circ as structural Verilog
// mp4_2
module multiplexer_4_2 (
  input  _0A0,
  input  _0A1,
  input  _0A2,
  input  _0A3,
  input  _1A0,
  input  _1A1,
  input  _1A2,
  input  _1A3,
  input  S1,
  input  S0,
  output _0Y,
  output _1Y
);

  wire and_1_out, and_2_out, and_3_out, and_4_out, and_5_out, and_6_out, and_7_out, and_8_out, not_1_out,
       not_2_out;

  not not_1 (not_1_out, S1);
  not not_2 (not_2_out, S0);
  and and_1 (and_1_out, not_1_out, not_2_out, _0A0);
  and and_2 (and_2_out, not_1_out, S0, _0A1);
  and and_3 (and_3_out, S1, not_2_out, _0A2);
  and and_4 (and_4_out, S1, S0, _0A3);
  and and_5 (and_5_out, not_1_out, not_2_out, _1A0);
  and and_6 (and_6_out, not_1_out, S0, _1A1);
  and and_7 (and_7_out, S1, not_2_out, _1A2);
  and and_8 (and_8_out, S1, S0, _1A3);
  or or_1 (_0Y, and_1_out, and_2_out, and_3_out, and_4_out);
  or or_2 (_1Y, and_5_out, and_6_out, and_7_out, and_8_out);
endmodule

module test (
  input  S0___S1,
  input  in_2,
  input  in_3,
  input  A____B____C____D,
  input  in_5,
  input  in_6,
  input  RESET,
  input  MSB,
  input  in_9,
  input  LSB,
  input  in_11
);

  wire clock_1_out, count_4_1_q0, count_4_1_q1, count_4_1_q2, count_4_1_q3, d_ff_1_q, fa_4_1_co, fa_4_1_s0,
       fa_4_1_s1, fa_4_1_s2, fa_4_1_s3, multiplexer_4_2_1__0y, multiplexer_4_2_1__1y, multiplexer_4_2_2__0y,
       multiplexer_4_2_2__1y, reg_4_1_q0, reg_4_1_q1, reg_4_1_q2, reg_4_1_q3, reg_4_2_q0, reg_4_2_q1,
       reg_4_2_q2, reg_4_2_q3, reg_4_3_q0, reg_4_3_q1, reg_4_3_q2, reg_4_3_q3;

  count_4 count_4_1 (
    .D0(fa_4_1_s0), .D1(fa_4_1_s1), .D2(fa_4_1_s2), .D3(fa_4_1_s3), .L(in_6), .CK(clock_1_out), .RST(RESET),
    .Q3(count_4_1_q3), .Q2(count_4_1_q2), .Q1(count_4_1_q1), .Q0(count_4_1_q0));
  Clock clock_1 (.out(clock_1_out));
  LED led_1 (.in(reg_4_1_q3));
  reg_4 reg_4_1 (
    .D0(fa_4_1_s0), .D1(fa_4_1_s1), .D2(fa_4_1_s2), .D3(fa_4_1_s3), .Q0(reg_4_1_q0), .Q1(reg_4_1_q1),
    .Q2(reg_4_1_q2), .Q3(reg_4_1_q3), .L(in_3), .CK(clock_1_out), .R0(RESET));  // open: R1
  LED led_2 (.in(reg_4_2_q3));
  reg_4 reg_4_2 (
    .D0(fa_4_1_s0), .D1(fa_4_1_s1), .D2(fa_4_1_s2), .D3(fa_4_1_s3), .Q0(reg_4_2_q0), .Q1(reg_4_2_q1),
    .Q2(reg_4_2_q2), .Q3(reg_4_2_q3), .L(A____B____C____D), .CK(clock_1_out), .R0(RESET));  // open: R1
  LED led_3 (.in(reg_4_3_q3));
  reg_4 reg_4_3 (
    .D0(fa_4_1_s0), .D1(fa_4_1_s1), .D2(fa_4_1_s2), .D3(fa_4_1_s3), .Q0(reg_4_3_q0), .Q1(reg_4_3_q1),
    .Q2(reg_4_3_q2), .Q3(reg_4_3_q3), .L(in_5), .CK(clock_1_out), .R0(RESET));  // open: R1
  LED led_4 (.in(count_4_1_q3));
  LED led_5 (.in(reg_4_1_q2));
  LED led_6 (.in(reg_4_1_q0));
  LED led_7 (.in(reg_4_1_q1));
  LED led_8 (.in(reg_4_2_q0));
  LED led_9 (.in(reg_4_2_q1));
  LED led_10 (.in(reg_4_2_q2));
  LED led_11 (.in(reg_4_3_q1));
  LED led_12 (.in(reg_4_3_q0));
  LED led_13 (.in(reg_4_3_q2));
  LED led_14 (.in(count_4_1_q1));
  LED led_15 (.in(count_4_1_q2));
  LED led_16 (.in(count_4_1_q0));
  multiplexer_4_2 multiplexer_4_2_1 (
    ._0A0(reg_4_1_q0), ._0A1(reg_4_2_q0), ._0A2(reg_4_3_q0), ._0A3(1'b0), .S1(S0___S1), .S0(in_2),
    ._0Y(multiplexer_4_2_1__0y), ._1Y(multiplexer_4_2_1__1y), ._1A0(reg_4_1_q1), ._1A1(reg_4_2_q1),
    ._1A2(reg_4_3_q1), ._1A3(1'b0));
  multiplexer_4_2 multiplexer_4_2_2 (
    ._0A0(reg_4_1_q2), ._0A1(reg_4_2_q2), ._0A2(reg_4_3_q2), ._0A3(1'b0), .S1(S0___S1), .S0(in_2),
    ._0Y(multiplexer_4_2_2__0y), ._1Y(multiplexer_4_2_2__1y), ._1A0(reg_4_1_q3), ._1A1(reg_4_2_q3),
    ._1A2(reg_4_3_q3), ._1A3(1'b0));
  FA_4 fa_4_1 (
    .A0(multiplexer_4_2_1__0y), .B0(in_11), .A1(multiplexer_4_2_1__1y), .B1(LSB), .A2(multiplexer_4_2_2__0y),
    .B2(in_9), .A3(multiplexer_4_2_2__1y), .B3(MSB), .S0(fa_4_1_s0), .S1(fa_4_1_s1), .S2(fa_4_1_s2),
    .S3(fa_4_1_s3), .Co(fa_4_1_co));  // open: Ci
  LED led_17 (.in(d_ff_1_q));
  D_Flip_Flop d_ff_1 (.clk(clock_1_out), .D(fa_4_1_co), .Q(d_ff_1_q));  // open: Qn, preset, en, reset

  // Notes on the sheet:
  //   LOAD
  //   REG[A]
  //   REG[B]
  //   REG[C]
  //   REG[D]
  //   CLOCK
  //   SELECTOR
  //   immediate
  //   ALU(今はただの全加算器)
  //   carry flag
endmodule

module reg_4 (
  input  D0,
  input  D1,
  input  D2,
  input  D3,
  input  L,
  input  CK,
  input  R1,
  input  R0,
  output Q0,
  output Q1,
  output Q2,
  output Q3
);

  wire d_ff_1_q, d_ff_2_q, d_ff_3_q, d_ff_4_q, multiplexer_2_1_y, multiplexer_2_2_y, multiplexer_2_3_y,
       multiplexer_2_4_y, not_1_out, or_1_out, or_2_out, or_3_out, or_4_out;

  multiplexer_2 multiplexer_2_1 (.A1(Q0), .A2(D0), .S(L), .Y(multiplexer_2_1_y));
  multiplexer_2 multiplexer_2_2 (.A1(Q1), .A2(D1), .S(L), .Y(multiplexer_2_2_y));
  multiplexer_2 multiplexer_2_3 (.A1(Q2), .A2(D2), .S(L), .Y(multiplexer_2_3_y));
  multiplexer_2 multiplexer_2_4 (.A1(Q3), .A2(D3), .S(L), .Y(multiplexer_2_4_y));
  D_Flip_Flop d_ff_1 (.clk(CK), .D(multiplexer_2_1_y), .Q(d_ff_1_q));  // open: Qn, preset, en, reset
  or or_1 (or_1_out, d_ff_1_q, R1);
  D_Flip_Flop d_ff_2 (.clk(CK), .D(multiplexer_2_2_y), .Q(d_ff_2_q));  // open: Qn, preset, en, reset
  or or_2 (or_2_out, d_ff_2_q, R1);
  D_Flip_Flop d_ff_3 (.clk(CK), .D(multiplexer_2_3_y), .Q(d_ff_3_q));  // open: Qn, preset, en, reset
  or or_3 (or_3_out, d_ff_3_q, R1);
  D_Flip_Flop d_ff_4 (.clk(CK), .D(multiplexer_2_4_y), .Q(d_ff_4_q));  // open: Qn, preset, en, reset
  or or_4 (or_4_out, d_ff_4_q, R1);
  not not_1 (not_1_out, R0);
  and and_1 (Q0, or_1_out, not_1_out);
  and and_2 (Q1, or_2_out, not_1_out);
  and and_3 (Q2, or_3_out, not_1_out);
  and and_4 (Q3, or_4_out, not_1_out);
endmodule

// mp_2
module multiplexer_2 (
  input  A1,
  input  A2,
  input  S,
  output Y
);

  wire and_1_out, and_2_out, not_1_out;

  not not_1 (not_1_out, S);
  and and_1 (and_1_out, not_1_out, A1);
  and and_2 (and_2_out, S, A2);
  or or_1 (Y, and_1_out, and_2_out);
endmodule

module _4bit_7seg (
  input  A0,
  input  A1,
  input  A2,
  input  A3,
  output Y0,
  output Y1,
  output Y2,
  output Y3,
  output Y4,
  output Y5,
  output Y6,
  output Y7
);

  _7_Segment_Display u_7_segment_display_1 ();  // open: g, f, a, b, e, d, c, dp
endmodule

module HA (
  input  A,
  input  B,
  output S,
  output C
);

  wire not_1_out, or_1_out;

  or or_1 (or_1_out, A, B);
  not not_1 (not_1_out, C);
  and and_1 (C, A, B);
  and and_2 (S, or_1_out, not_1_out);
endmodule

module FA (
  input  Ci,
  input  A,
  input  B,
  output S,
  output Co
);

  wire ha_1_c, ha_1_s, ha_2_c;

  HA ha_1 (.A(A), .B(B), .S(ha_1_s), .C(ha_1_c));
  HA ha_2 (.A(Ci), .B(ha_1_s), .S(S), .C(ha_2_c));
  or or_1 (Co, ha_2_c, ha_1_c);
endmodule

module FA_4 (
  input  Ci,
  input  A0,
  input  B0,
  input  A1,
  input  B1,
  input  A2,
  input  B2,
  input  A3,
  input  B3,
  output S0,
  output S1,
  output S2,
  output S3,
  output Co
);

  wire fa_1_co, fa_2_co, fa_3_co;

  FA fa_1 (.Ci(Ci), .A(A0), .B(B0), .S(S0), .Co(fa_1_co));
  FA fa_2 (.Ci(fa_1_co), .A(A1), .B(B1), .S(S1), .Co(fa_2_co));
  FA fa_3 (.Ci(fa_2_co), .A(A2), .B(B2), .S(S2), .Co(fa_3_co));
  FA fa_4 (.Ci(fa_3_co), .A(A3), .B(B3), .S(S3), .Co(Co));
endmodule

module count_4 (
  input  D0,
  input  D1,
  input  D2,
  input  D3,
  input  L,
  input  CK,
  input  RST,
  output Q3,
  output Q2,
  output Q1,
  output Q0
);

  wire fa_4_1_s0, fa_4_1_s1, fa_4_1_s2, fa_4_1_s3, multiplexer_4_2_1__0y, multiplexer_4_2_1__1y,
       multiplexer_4_2_2__0y, multiplexer_4_2_2__1y, not_1_out;

  multiplexer_4_2 multiplexer_4_2_1 (
    ._0A0(fa_4_1_s0), ._0A1(D0), .S1(1'b0), .S0(L), ._0Y(multiplexer_4_2_1__0y), ._1Y(multiplexer_4_2_1__1y),
    ._1A0(fa_4_1_s1), ._1A1(D1));  // open: _0A2, _0A3, _1A2, _1A3
  multiplexer_4_2 multiplexer_4_2_2 (
    ._0A0(fa_4_1_s2), ._0A1(D2), .S1(1'b0), .S0(L), ._0Y(multiplexer_4_2_2__0y), ._1Y(multiplexer_4_2_2__1y),
    ._1A0(fa_4_1_s3), ._1A1(D3));  // open: _0A2, _0A3, _1A2, _1A3
  not not_1 (not_1_out, RST);
  reg_4 reg_4_1 (
    .D0(multiplexer_4_2_1__0y), .D1(multiplexer_4_2_1__1y), .D2(multiplexer_4_2_2__0y),
    .D3(multiplexer_4_2_2__1y), .Q0(Q0), .Q1(Q1), .Q2(Q2), .Q3(Q3), .L(not_1_out), .CK(CK), .R0(RST));  // open: R1
  LED led_1 (.in(Q1));
  LED led_2 (.in(Q0));
  LED led_3 (.in(Q3));
  LED led_4 (.in(Q2));
  FA_4 fa_4_1 (
    .A0(Q0), .B0(1'b1), .A1(Q1), .B1(1'b0), .A2(Q2), .B2(1'b0), .A3(Q3), .B3(1'b0), .S0(fa_4_1_s0),
    .S1(fa_4_1_s1), .S2(fa_4_1_s2), .S3(fa_4_1_s3));  // open: Ci, Co
endmodule
